# Fritzing sketch PINBruteforcer2 (saved by Fritzing 0.9.3b)
breadboards: 1

parts:
  Componente1 = Arduino Leonardo (Rev3b)
  USBTTL1 = USB TTL Serial Cable  # not connected
  S1 = Pushbutton [package="[SMD]"]
  R1 = Resistor [tolerance=±5% resistance=220 package=THT]

nets:
  N1: Componente1.D7, S1.Pin_3, S1.Pin_4, R1.Pin_1
  N2: Componente1.GND, R1.Pin_0
  N3: S1.Pin_1, S1.Pin_2

notes:
  OTG CABLE
